# Fritzing sketch led circuit (saved by Fritzing 0.9.3b)
breadboards: 1

parts:
  Part1 = Arduino Uno (Rev3)
  R1 = Resistor [tolerance=±5% resistance=220 package=THT]
  LED1 = LED - 5mm [color="Red (633nm)" package="5 mm [THT]"]

nets:
  N1: Part1.D5_PWM, LED1.cathode
  N2: Part1.5V, R1.Pin_1
  N3: R1.Pin_0, LED1.anode
