# Fritzing sketch switch circuit (saved by Fritzing 0.9.3b)
breadboards: 1

parts:
  Part1 = Arduino Uno (Rev3)
  R1 = Resistor [tolerance=±5% resistance=220 package=THT]
  LED1 = LED - 5mm [color="Red (633nm)" package="5 mm [THT]"]
  S1 = Pushbutton [package="[THT]"]
  S2 = Pushbutton [package="[THT]"]

nets:
  N1: Part1.D3_PWM, S2.Pin_1, S2.Pin_2
  N2: Part1.D4, S1.Pin_1, S1.Pin_2
  N3: Part1.D5_PWM, LED1.cathode
  N4: Part1.5V, R1.Pin_1
  N5: Part1.GND, S1.Pin_3, S1.Pin_4, S2.Pin_3, S2.Pin_4
  N6: R1.Pin_0, LED1.anode
