# Fritzing sketch seven segment (saved by Fritzing 0.9.3b)
breadboards: 1
perfboards: 1

parts:
  Part1 = Arduino Uno (Rev3) - ICSP
  R1 = Resistor [tolerance=±5% resistance=220 package=THT]
  R2 = Resistor [tolerance=±5% resistance=220 package=THT]
  R3 = Resistor [tolerance=±5% resistance=220 package=THT]
  R4 = Resistor [tolerance=±5% resistance=220 package=THT]
  R5 = Resistor [tolerance=±5% resistance=220 package=THT]
  DI1 = 7-Segment LED Display [package=THT]  # not connected
  DI2 = 7-Segment LED Display [package=THT]  # not connected
  DI3 = 7-Segment LED Display [package=THT]
  DI4 = 7-Segment LED Display [package=THT]  # not connected
  DI5 = 7-Segment LED Display [package=THT]
  DI6 = 7-Segment LED Display [package=THT]  # not connected
  R6 = Resistor [tolerance=±5% resistance=220 package=THT]

nets:
  N1: Part1.A0, R5.Pin_1
  N2: Part1.A1, R4.Pin_1
  N3: Part1.D10_PWM/SS, R1.Pin_1
  N4: Part1.D11_PWM/MOSI, R6.Pin_1
  N5: Part1.D12/MISO, R2.Pin_1
  N6: Part1.D13/SCK, R3.Pin_1
  N7: DI3.cathodeDP, DI5.cathodeE
  N8: DI3.cathodeB, DI5.cathodeG

notes:
  g
  a
  b
  c
  d
  dp
  d1
  e
  f
  d2
  d3
  d4
  d5
  d6
